# Fritzing sketch thermostat-bb2 (saved by Fritzing 0.9.3b)
perfboards: 1

parts:
  Part1 = Arduino Nano (Rev3.0) (ICSP)
  J1 = Screw terminal - 2 pins [package=THT]
  R1 = Resistor [tolerance=±5% resistance=4.7k package=THT]
  DIP-Relay1 = DIP-Relay-D31A [part_number=D31A*]
  J2 = shrouded pin header, 16 pins [form="♂ (shrouded male)"]
  J3 = Screw terminal - 2 pins [package=THT]
  R3 = Resistor [tolerance=±5% resistance=1k package=THT]
  R4 = Resistor [tolerance=±5% resistance=1k package=THT]
  R5 = Resistor [tolerance=±5% resistance=1k package=THT]
  J4 = Screw terminal - 2 pins [package=THT]  # not connected
  J5 = Screw terminal - 2 pins [package=THT]  # not connected

nets:
  N1: Part1.GND, DIP-Relay1.Coil2_-, J2.pin1, J2.pin3, J2.pin9, J3.pin1, R3.Pin_1
  N2: Part1.D2, J2.pin10
  N3: Part1.D3, J2.pin7
  N4: Part1.D4, J2.pin11
  N5: Part1.D5, J2.pin6
  N6: Part1.D7, R1.Pin_0, J3.pin2
  N7: Part1.D8, DIP-Relay1.COIL1_+
  N8: Part1.D11/MOSI, J2.pin14
  N9: Part1.D12/MISO, J2.pin15
  N10: Part1.5V, R1.Pin_1, J2.pin16, R5.Pin_0
  N11: J1.pin1, DIP-Relay1.B2_Switch_Terminal_B
  N12: J1.pin2, DIP-Relay1.A2_Switch_Terminal_A
  N13: J2.pin2, R4.Pin_1
  N14: J2.pin8, R5.Pin_1
  N15: R3.Pin_0, R4.Pin_0

custom parts:
  Arduino Nano (Rev3.0) (ICSP): The Arduino Nano is a small, complete, and breadboard-friendly board based on the ATmega328 (Arduino Nano 3.0) or ATmega168 (Arduino Nano 2.x). It has more or less the same functionality of the Arduino Duemilanove, but in a different package. It lacks only a DC power jack, and works with a Mini-B USB cable instead of a standard one. The Nano was designed and is being produced by Gravitech.
